# Fritzing sketch Fotoresistencia (saved by Fritzing 0.9.3b)
breadboards: 1

parts:
  R1 = Resistor [tolerance=±5% resistance=220 package="0805 [SMD]"]
  R2 = PHOTOCELL [package=photocell-kit]
  Componente1 = Arduino Uno (Rev3)

nets:
  N1: R1.Pin_0, R2.P$2, Componente1.A1
