# Fritzing sketch Ball Switch (saved by Fritzing 0.9.3b)

parts:
  Componente1 = Arduino Uno (Rev3)
  Mod1 = KY-020 Tilt Switch Module [package="Breakout board"]

nets:
  N1: Componente1.D8, Mod1.S
  N2: Componente1.GND, Mod1.-
  5V: Componente1.5V, Mod1.Vin

custom parts:
  KY-020 Tilt Switch Module: KY-020 tilt switch sensor module. Closes the circuit when it is tilted to the side as long as it is moved with enough force and degree of inclination to activate the ball switch inside.
