# Fritzing sketch Sensor SmallSound (saved by Fritzing 0.9.3b)
breadboards: 1

parts:
  Part1 = KY-037 High Sensitivity Sound Detection Module [package="Breakout board"]
  Componente1 = Arduino Uno (Rev3)

nets:
  N1: Part1.A0, Componente1.D10_PWM/SS
  N2: Part1.G, Componente1.GND
  N3: Part1.+, Componente1.5V

custom parts:
  KY-037 High Sensitivity Sound Detection Module: KY-037 high sensitivity sound detection module is an analog/digital sensor that uses a condenser microphone to observe changes in environment noise.
