# Fritzing sketch Heartbeat (saved by Fritzing 0.9.3b)

parts:
  SEN1 = Pulse Sensor [package=SIP]  # not connected
  SEN2 = Pulse Sensor [package=SIP]
  esp1 = ESP32 DevKitc V4

nets:
  VCC: SEN2.Vcc, esp1.5V
  GND: SEN2.GND, esp1.GND
  N1: SEN2.Signal, esp1.IO14

custom parts:
  Pulse Sensor: Pulse Sensor Optical Heart Rate Monitor for Arduino and other microcontrollers
  Pulse Sensor: Pulse Sensor Optical Heart Rate Monitor for Arduino and other microcontrollers
  ESP32 DevKitc V4: ESP32-DevKitC board with ESP32-WROOM-32 module. ESP32-DevKitC V4 is a small-sized ESP32-based development board produced by Espressif. Most of the pins on the ESP module are broken out to the pin headers on the board. The pins D0, D1, D2, D3, CMD and CLK are used internally for communication between ESP32 and SPI flash memory. They are grouped on both sides near the USB connector. Avoid using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
