# Fritzing sketch Ball Switch con Motor Corriente Continua (saved by Fritzing 0.9.3b)

parts:
  S1 = H-Bridge with L298N
  M1 = DC Motor
  Componente1 = Arduino Uno (Rev3)
  Mod1 = KY-020 Tilt Switch Module [package="Breakout board"]

nets:
  12V: S1.12V, Componente1.5V
  GND: S1.GND, Componente1.GND, Mod1.-
  N1: S1.IN4, Componente1.D3_PWM
  N2: S1.M2-01, M1.pin_2
  N3: S1.M2-02, M1.pin_1
  N4: Componente1.D12/MISO, Mod1.S
  3V3: Componente1.3V3, Mod1.Vin

custom parts:
  H-Bridge with L298N: h-bridge
  KY-020 Tilt Switch Module: KY-020 tilt switch sensor module. Closes the circuit when it is tilted to the side as long as it is moved with enough force and degree of inclination to activate the ball switch inside.
