# Fritzing sketch Sensor de inclinación SW-520D con Servo Motor (saved by Fritzing 0.9.3b)
breadboards: 1

parts:
  Componente1 = Arduino Uno (Rev3)
  J1 = Basic Servo
  Mod1 = KY-020 Tilt Switch Module [package="Breakout board"]

nets:
  N1: Componente1.D8, Mod1.S
  N2: Componente1.D10_PWM/SS, J1.pulse
  5V: Componente1.5V, J1.vcc, Mod1.Vin
  GND: Componente1.GND, J1.gnd, Mod1.-

custom parts:
  KY-020 Tilt Switch Module: KY-020 tilt switch sensor module. Closes the circuit when it is tilted to the side as long as it is moved with enough force and degree of inclination to activate the ball switch inside.
