# Fritzing sketch Sensor de inclinación KY-017 con Motor paso a paso (saved by Fritzing 0.9.3b)
breadboards: 1

parts:
  Driver1 = 28BYJ-48 Driver Module [part_number=ULN2003 package=THT]
  SM1 = 28BYJ-48 Stepper Motor [part_number=28BYJ-48]
  Componente1 = Arduino Uno (Rev3)
  Mod1 = KY-017 Mercury Tilt Switch [package="Breakout board"]

nets:
  N1: Driver1.IN1, Componente1.D11_PWM/MOSI
  N2: Driver1.IN2, Componente1.D10_PWM/SS
  N3: Driver1.IN3, Componente1.D9_PWM
  N4: Driver1.IN4, Componente1.D8
  N5: Driver1.blue-pin, SM1.blue-pin
  N6: Driver1.pink-pin, SM1.pink-pin
  N7: Driver1.yellow-pin, SM1.yellow-pin
  N8: Driver1.orange-pin, SM1.orange-pin
  N9: Driver1.red-pin, SM1.red-pin
  N10: Componente1.D7, Mod1.S
  5V: Componente1.5V, Mod1.Vin
  N11: Componente1.GND, Mod1.-

custom parts:
  28BYJ-48 Driver Module: ULN2003 Driver Module for the 28BYJ-48 Unipolar Stepper Motor LED A - Blue wire - Bottom coil left LED B - Pink wire - Top coil left LED C - Yellow wire - Bottom coil right LED D - Orange wire - Top coil right Common rail - red Connector pins: blue - pink - yellow - orange - red Control pins - IN1 to IN4 Power pins - GND & Vmotor (5-12V) On/Off jumper (if removed, power to motor is cut).
  28BYJ-48 Stepper Motor: Unipolar Stepper Motor 28BYJ-48 Top coil - pink & orange Bottom coil - blue & yellow Common rail - red Connector pins: blue - pink - yellow - orange - red
  KY-017 Mercury Tilt Switch: KY-017 mercury tilt switch module, it uses a small mercury ball that completes the circuit when you tilt the module.
