# Fritzing sketch Modulo Digital Display con Encoder rotativo (saved by Fritzing 0.9.3b)

parts:
  RE3 = KY-040 Rotary encoder [package=THT]
  Display2 = 4-Digit 7-segment LED Display [package=THT]
  esp1 = ESP32 DevKitc V4

nets:
  N1: RE3.GND, esp1.GND#32
  N2: RE3.Vcc, esp1.VN
  N3: RE3.DT, esp1.IO15
  N4: RE3.CLK, esp1.IO2
  VCC: Display2.VCC, esp1.5V
  N5: Display2.GND, esp1.GND#12
  N6: Display2.DIO, esp1.IO5
  N7: Display2.CLK, esp1.IO4

custom parts:
  KY-040 Rotary encoder: KY-040 Rotary Encoder with switch on breakout borad from AZ Delivery
  4-Digit 7-segment LED Display: A 4-digit 7-segments LED display PCB module driven by a TM1637 control IC via 1-wire protocol.
  ESP32 DevKitc V4: ESP32-DevKitC board with ESP32-WROOM-32 module. ESP32-DevKitC V4 is a small-sized ESP32-based development board produced by Espressif. Most of the pins on the ESP module are broken out to the pin headers on the board. The pins D0, D1, D2, D3, CMD and CLK are used internally for communication between ESP32 and SPI flash memory. They are grouped on both sides near the USB connector. Avoid using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
