# Fritzing sketch Heartbeat Sensor con Pantalla 0.96 IPS LCD (saved by Fritzing 0.9.3b)
breadboards: 1

parts:
  SEN1 = Pulse Sensor [package=SIP]
  Componente1 = Arduino Uno (Rev3)
  OLED1 = OLED 128x64 I2C Monochrome Display GND-VDD

nets:
  VCC: SEN1.Vcc, Componente1.3V3
  GND: SEN1.GND, Componente1.GND, OLED1.GND
  N1: SEN1.Signal, Componente1.A0
  N2: Componente1.D10_PWM/SS, OLED1.SCK
  N3: Componente1.D11_PWM/MOSI, OLED1.SDA
  5V: Componente1.5V, OLED1.VDD

custom parts:
  Pulse Sensor: Pulse Sensor Optical Heart Rate Monitor for Arduino and other microcontrollers
  OLED 128x64 I2C Monochrome Display GND-VDD: OLED 128x64 I2C Monochrome Display. Note: there are two variants of this part, this one is the GND VDD SCK SDA variant. The other is VDD GND SCK SDA. Make sure you select the part that matches your module as using the incorrect part will probably destroy your module! In addition the mounting holes are marked on silkscreen but not by default drilled. If you want drilled mounting holes, copy a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
